# Fritzing sketch genius_esp32 (saved by Fritzing 0.9.10b)
breadboards: 2

parts:
  R1 = Resistor [tolerance=±5% power=0.25 resistance=220 package=THT]
  R2 = Resistor [tolerance=±5% power=0.25 resistance=220 package=THT]
  R3 = Resistor [tolerance=±5% power=0.25 resistance=220 package=THT]
  R4 = Resistor [tolerance=±5% power=0.25 resistance=220 package=THT]
  LED1 = LED - 5mm [color="Red (633nm)" current=0.030 package="5 mm [THT]"]
  LED2 = LED - 5mm [color="Green (555nm)" current=0.030 package="5 mm [THT]"]
  LED3 = LED - 5mm [color="Blue (430nm)" current=0.030 package="5 mm [THT]"]
  LED4 = LED - 5mm [color="Yellow (574nm)" current=0.030 package="5 mm [THT]"]
  S1 = Pushbutton [package="[THT]"]
  S2 = Pushbutton [package="[THT]"]
  S3 = Pushbutton [package="[THT]"]
  S4 = Pushbutton [package="[THT]"]
  R5 = Resistor [tolerance=±5% power=0.25 resistance=10k package=THT]
  R6 = Resistor [tolerance=±5% power=0.25 resistance=10k package=THT]
  R7 = Resistor [tolerance=±5% power=0.25 resistance=10k package=THT]
  R8 = Resistor [tolerance=±5% power=0.25 resistance=10k package=THT]
  U1 = ESP32-38PinWide [part_number=ESP32-38PinWide]
  J1 = Piezo Speaker
  OLED1 = OLED 128x64 I2C Monochrome Display

nets:
  N1: R1.Pin_0, U1.GPIO18
  N2: R1.Pin_1, LED1.cathode
  N3: R2.Pin_0, U1.GPIO17
  N4: R2.Pin_1, LED2.cathode
  N5: R3.Pin_0, U1.GPIO16
  N6: R3.Pin_1, LED3.cathode
  N7: R4.Pin_0, U1.GPIO15
  N8: R4.Pin_1, LED4.cathode
  GND: LED1.anode, LED2.anode, LED3.anode, LED4.anode, R5.Pin_1, R6.Pin_1, R7.Pin_1, R8.Pin_1, U1.GND, J1.pin1, OLED1.GND
  N9: S1.Pin_1, S1.Pin_2, R5.Pin_0, U1.GPIO19
  3.3V: S1.Pin_3, S1.Pin_4, S2.Pin_3, S2.Pin_4, S3.Pin_3, S3.Pin_4, S4.Pin_3, S4.Pin_4, U1.3.3, OLED1.VDD
  N10: S2.Pin_1, S2.Pin_2, R6.Pin_0, U1.GPIO21
  N11: S3.Pin_1, S3.Pin_2, R7.Pin_0, U1.GPIO22
  N12: S4.Pin_1, S4.Pin_2, R8.Pin_0, U1.GPIO23
  N13: U1.GPIO25, OLED1.SDA
  N14: U1.GPIO26, OLED1.SCK
  N15: U1.GPIO14, J1.pin2

custom parts:
  ESP32-38PinWide: Generic 38-Pin ESP32 with wide format (only access to one side of pins on a breadboard) based on Stephen Lilley's HiLetgo ESP-WROOM-32 ESP32 ESP-32S Development Board.
